// Logisim project 74155_74191_shmmy.circ as structural Verilog: 2 circuits, main circuit L_74155_decoder
// 74155
module L_74155_decoder (
  input  L_1_1C_53a349fb,
  input  L_2_1_G_cf5544c9,
  input  L_15_2_C_07cd6f28,
  input  L_3_B_7bfc90cd,
  input  L_14_2_G_27a5655c,
  input  L_13_A_3cb1ee42,
  output L_16_Vcc_f510297a,
  output L_4_1Y3_de179552,
  output L_5_1Y2_dcf02d34,
  output L_12_2Y3_5ba70a88,
  output L_6_1Y1_7ce8080f,
  output L_11_2Y2_1070e5ad,
  output L_7_1Y0_86881f2f,
  output L_10_2Y1_9a0a73bb,
  output L_8_GND_c4034234,
  output L_9_2Y0_bd221ec9
);

  wire demultiplexer_1_out0, demultiplexer_1_out1, demultiplexer_1_out2, demultiplexer_1_out3,
       demultiplexer_2_out0, demultiplexer_2_out1, demultiplexer_2_out2, demultiplexer_2_out3, not_5_out,
       not_6_out, not_7_out;

  not not_1 (L_4_1Y3_de179552, demultiplexer_1_out3);
  not not_2 (L_5_1Y2_dcf02d34, demultiplexer_1_out2);
  not not_3 (L_6_1Y1_7ce8080f, demultiplexer_1_out1);
  not not_4 (L_7_1Y0_86881f2f, demultiplexer_1_out0);
  not not_5 (not_5_out, L_2_1_G_cf5544c9);
  Demultiplexer #(.enable("true"), .select(2)) demultiplexer_1 (
    .out0(demultiplexer_1_out0), .out1(demultiplexer_1_out1), .out2(demultiplexer_1_out2),
    .out3(demultiplexer_1_out3), .in(L_1_1C_53a349fb), .sel({L_3_B_7bfc90cd, L_13_A_3cb1ee42}), .en(not_5_out));
  Demultiplexer #(.enable("true"), .select(2)) demultiplexer_2 (
    .out0(demultiplexer_2_out0), .out1(demultiplexer_2_out1), .out2(demultiplexer_2_out2),
    .out3(demultiplexer_2_out3), .in(not_6_out), .sel({L_3_B_7bfc90cd, L_13_A_3cb1ee42}), .en(not_7_out));
  not not_6 (not_6_out, L_15_2_C_07cd6f28);
  not not_7 (not_7_out, L_14_2_G_27a5655c);
  not not_8 (L_12_2Y3_5ba70a88, demultiplexer_2_out3);
  not not_9 (L_11_2Y2_1070e5ad, demultiplexer_2_out2);
  not not_10 (L_10_2Y1_9a0a73bb, demultiplexer_2_out1);
  not not_11 (L_9_2Y0_bd221ec9, demultiplexer_2_out0);

  assign L_8_GND_c4034234 = 1'b0;
  assign L_16_Vcc_f510297a = 1'b1;

  // Notes on the sheet:
  //   74155: Dual 2-to-4 Line Decoder/DeMux (Invert)
endmodule

// 74191
module L_74191_counter (
  input  L_14_CLK_e9d592e6,
  input  L_5_D_U_17f665bf,
  input  L_4_CTEN_2e22b794,
  input  L_15_A_f9b503e3,
  input  L_1_B_ec77ed50,
  input  L_10_C_7280f7fb,
  input  L_9_D_8c39df1c,
  input  L_11_LOAD_a61801b1,
  output L_13_RCO_37260826,
  output L_12_MAX_MIN_34a3284e,
  output L_3_QA_56e81b3a,
  output L_2_QB_1d9e6957,
  output L_6_QC_20e0091a,
  output L_16_Vcc_f510297a,
  output L_8_GND_c4034234,
  output L_7_QD_727f0350
);

  wire and_1_out, and_2_out, and_3_out, and_4_out, and_5_out, and_6_out, and_7_out, and_8_out, and_9_out,
       and_10_out, and_11_out, and_12_out, and_13_out, and_14_out, and_15_out, and_16_out, j_k_ff_1_qn,
       j_k_ff_2_qn, j_k_ff_3_qn, j_k_ff_4_qn, nor_1_out, nor_2_out, not_1_out, not_2_out, not_3_out,
       not_4_out, or_2_out, or_3_out, or_4_out;

  not not_1 (not_1_out, L_14_CLK_e9d592e6);
  not not_2 (not_2_out, L_5_D_U_17f665bf);
  nor nor_1 (nor_1_out, L_5_D_U_17f665bf, L_4_CTEN_2e22b794);
  nor nor_2 (nor_2_out, L_4_CTEN_2e22b794, not_2_out);
  not not_3 (not_3_out, L_11_LOAD_a61801b1);
  and and_1 (and_1_out, not_2_out, L_7_QD_727f0350, L_6_QC_20e0091a, L_2_QB_1d9e6957, L_3_QA_56e81b3a);
  or or_1 (L_12_MAX_MIN_34a3284e, and_1_out, and_2_out);
  and and_2 (and_2_out, L_5_D_U_17f665bf, j_k_ff_4_qn, j_k_ff_3_qn, j_k_ff_2_qn, j_k_ff_1_qn);
  not not_4 (not_4_out, L_4_CTEN_2e22b794);
  and and_3 (and_3_out, nor_2_out, j_k_ff_1_qn);
  or or_2 (or_2_out, and_3_out, and_4_out);
  and and_4 (and_4_out, L_3_QA_56e81b3a, nor_1_out);
  and and_5 (and_5_out, nor_2_out, j_k_ff_1_qn, j_k_ff_2_qn);
  or or_3 (or_3_out, and_5_out, and_6_out);
  and and_6 (and_6_out, L_3_QA_56e81b3a, L_2_QB_1d9e6957, nor_1_out);
  and and_7 (and_7_out, nor_2_out, j_k_ff_1_qn, j_k_ff_2_qn, j_k_ff_3_qn);
  or or_4 (or_4_out, and_7_out, and_8_out);
  and and_8 (and_8_out, L_3_QA_56e81b3a, L_2_QB_1d9e6957, L_6_QC_20e0091a, nor_1_out);
  J_K_Flip_Flop j_k_ff_1 (
    .J(not_4_out), .K(not_4_out), .clk(not_1_out), .Q(L_3_QA_56e81b3a), .Qn(j_k_ff_1_qn), .preset(and_9_out),
    .reset(and_10_out));
  and and_9 (and_9_out, L_15_A_f9b503e3, not_3_out);
  and and_10 (and_10_out, ~and_9_out, not_3_out);  // AND_Gate
  and and_11 (and_11_out, L_1_B_ec77ed50, not_3_out);
  and and_12 (and_12_out, ~and_11_out, not_3_out);  // AND_Gate
  and and_13 (and_13_out, L_10_C_7280f7fb, not_3_out);
  and and_14 (and_14_out, ~and_13_out, not_3_out);  // AND_Gate
  and and_15 (and_15_out, L_9_D_8c39df1c, not_3_out);
  and and_16 (and_16_out, ~and_15_out, not_3_out);  // AND_Gate
  nand nand_1 (L_13_RCO_37260826, not_1_out, not_4_out, L_12_MAX_MIN_34a3284e);
  J_K_Flip_Flop j_k_ff_2 (
    .J(or_2_out), .K(or_2_out), .clk(not_1_out), .Q(L_2_QB_1d9e6957), .Qn(j_k_ff_2_qn), .preset(and_11_out),
    .reset(and_12_out));
  J_K_Flip_Flop j_k_ff_3 (
    .J(or_3_out), .K(or_3_out), .clk(not_1_out), .Q(L_6_QC_20e0091a), .Qn(j_k_ff_3_qn), .preset(and_13_out),
    .reset(and_14_out));
  J_K_Flip_Flop j_k_ff_4 (
    .J(or_4_out), .K(or_4_out), .clk(not_1_out), .Q(L_7_QD_727f0350), .Qn(j_k_ff_4_qn), .preset(and_15_out),
    .reset(and_16_out));

  assign L_8_GND_c4034234 = 1'b0;
  assign L_16_Vcc_f510297a = 1'b1;

  // Notes on the sheet:
  //   74191: Synchronous 4-bit Binary Up/Down Counter
endmodule
