// Logisim project project.circ as structural Verilog: 1 circuit, main circuit main
module main (
  output out_1,
  output out_2,
  output out_3,
  output out_4,
  output out_5
);

  wire button_1_out, button_2_out, clock_1_out, j_k_ff_1_qn, j_k_ff_2_q, l_74155_decoder_1_l_4_1y3_de179552,
       l_74155_decoder_1_l_5_1y2_dcf02d34, l_74155_decoder_1_l_6_1y1_7ce8080f,
       l_74155_decoder_1_l_7_1y0_86881f2f, l_74155_decoder_1_l_8_gnd_c4034234,
       l_74155_decoder_1_l_9_2y0_bd221ec9, l_74155_decoder_1_l_10_2y1_9a0a73bb,
       l_74155_decoder_1_l_11_2y2_1070e5ad, l_74155_decoder_1_l_12_2y3_5ba70a88,
       l_74155_decoder_1_l_16_vcc_f510297a, l_74191_counter_1_l_2_qb_1d9e6957,
       l_74191_counter_1_l_3_qa_56e81b3a, l_74191_counter_1_l_6_qc_20e0091a,
       l_74191_counter_1_l_7_qd_727f0350, l_74191_counter_1_l_8_gnd_c4034234,
       l_74191_counter_1_l_16_vcc_f510297a, l_74191_counter_2_l_8_gnd_c4034234,
       l_74191_counter_2_l_16_vcc_f510297a, nand_1_out, nor_1_out, nor_2_out, not_1_out, not_2_out,
       not_3_out, not_4_out, not_5_out, not_6_out, not_7_out, not_8_out, not_9_out, not_10_out, not_11_out,
       xor_1_out, xor_2_out;

  xor xor_1 (xor_1_out, l_74191_counter_1_l_6_qc_20e0091a, l_74191_counter_1_l_2_qb_1d9e6957);
  xor xor_2 (xor_2_out, l_74191_counter_1_l_2_qb_1d9e6957, l_74191_counter_1_l_3_qa_56e81b3a);
  nor nor_1 (nor_1_out, xor_1_out, xor_2_out);
  not not_1 (not_1_out, nor_1_out);
  nand nand_1 (nand_1_out, not_1_out, button_2_out);
  not not_2 (not_2_out, nand_1_out);
  Button button_1 (.out(button_1_out));
  nor nor_2 (nor_2_out, l_74191_counter_1_l_7_qd_727f0350, not_2_out);
  not not_3 (not_3_out, nor_2_out);
  J_K_Flip_Flop j_k_ff_1 (
    .J(1'b0), .K(1'b0), .clk(clock_1_out), .Q(out_5), .Qn(j_k_ff_1_qn), .preset(button_1_out),
    .reset(not_3_out));
  L_74155_decoder l_74155_decoder_1 (
    .L_1_1C_53a349fb(l_74191_counter_1_l_6_qc_20e0091a), .L_2_1_G_cf5544c9(j_k_ff_1_qn),
    .L_3_B_7bfc90cd(l_74191_counter_1_l_2_qb_1d9e6957),
    .L_15_2_C_07cd6f28(l_74191_counter_1_l_6_qc_20e0091a), .L_14_2_G_27a5655c(j_k_ff_1_qn),
    .L_13_A_3cb1ee42(l_74191_counter_1_l_3_qa_56e81b3a),
    .L_4_1Y3_de179552(l_74155_decoder_1_l_4_1y3_de179552),
    .L_5_1Y2_dcf02d34(l_74155_decoder_1_l_5_1y2_dcf02d34),
    .L_6_1Y1_7ce8080f(l_74155_decoder_1_l_6_1y1_7ce8080f),
    .L_7_1Y0_86881f2f(l_74155_decoder_1_l_7_1y0_86881f2f),
    .L_8_GND_c4034234(l_74155_decoder_1_l_8_gnd_c4034234),
    .L_16_Vcc_f510297a(l_74155_decoder_1_l_16_vcc_f510297a),
    .L_12_2Y3_5ba70a88(l_74155_decoder_1_l_12_2y3_5ba70a88),
    .L_11_2Y2_1070e5ad(l_74155_decoder_1_l_11_2y2_1070e5ad),
    .L_10_2Y1_9a0a73bb(l_74155_decoder_1_l_10_2y1_9a0a73bb),
    .L_9_2Y0_bd221ec9(l_74155_decoder_1_l_9_2y0_bd221ec9));
  LED led_1 (.in(not_4_out));
  LED led_2 (.in(not_5_out));
  not not_4 (not_4_out, l_74155_decoder_1_l_9_2y0_bd221ec9);
  not not_5 (not_5_out, l_74155_decoder_1_l_10_2y1_9a0a73bb);
  Clock clock_1 (.out(clock_1_out));
  LED led_3 (.in(not_6_out));
  LED led_4 (.in(not_7_out));
  LED led_5 (.in(not_8_out));
  not not_6 (not_6_out, l_74155_decoder_1_l_11_2y2_1070e5ad);
  not not_7 (not_7_out, l_74155_decoder_1_l_12_2y3_5ba70a88);
  not not_8 (not_8_out, l_74155_decoder_1_l_7_1y0_86881f2f);
  L_74191_counter l_74191_counter_1 (
    .L_5_D_U_17f665bf(j_k_ff_2_q), .L_4_CTEN_2e22b794(1'b0), .L_11_LOAD_a61801b1(out_5),
    .L_14_CLK_e9d592e6(clock_1_out), .L_16_Vcc_f510297a(l_74191_counter_1_l_16_vcc_f510297a),
    .L_8_GND_c4034234(l_74191_counter_1_l_8_gnd_c4034234),
    .L_3_QA_56e81b3a(l_74191_counter_1_l_3_qa_56e81b3a), .L_6_QC_20e0091a(l_74191_counter_1_l_6_qc_20e0091a),
    .L_7_QD_727f0350(l_74191_counter_1_l_7_qd_727f0350), .L_2_QB_1d9e6957(l_74191_counter_1_l_2_qb_1d9e6957));  // open: L_15_A_f9b503e3, L_1_B_ec77ed50, L_10_C_7280f7fb, L_9_D_8c39df1c, L_13_RCO_37260826, L_12_MAX_MIN_34a3284e
  Button button_2 (.out(button_2_out));
  LED led_6 (.in(not_9_out));
  LED led_7 (.in(not_10_out));
  LED led_8 (.in(not_11_out));
  not not_9 (not_9_out, l_74155_decoder_1_l_5_1y2_dcf02d34);
  not not_10 (not_10_out, l_74155_decoder_1_l_4_1y3_de179552);
  not not_11 (not_11_out, l_74155_decoder_1_l_6_1y1_7ce8080f);
  J_K_Flip_Flop j_k_ff_2 (
    .J(button_2_out), .K(button_2_out), .clk(clock_1_out), .Q(j_k_ff_2_q), .reset(not_3_out));  // open: Qn, preset
  L_74191_counter l_74191_counter_2 (
    .L_5_D_U_17f665bf(l_74191_counter_2_l_8_gnd_c4034234),
    .L_4_CTEN_2e22b794(l_74191_counter_2_l_8_gnd_c4034234), .L_11_LOAD_a61801b1(out_5),
    .L_14_CLK_e9d592e6(button_2_out), .L_16_Vcc_f510297a(l_74191_counter_2_l_16_vcc_f510297a),
    .L_8_GND_c4034234(l_74191_counter_2_l_8_gnd_c4034234), .L_3_QA_56e81b3a(out_4), .L_6_QC_20e0091a(out_2),
    .L_7_QD_727f0350(out_1), .L_2_QB_1d9e6957(out_3));  // open: L_15_A_f9b503e3, L_1_B_ec77ed50, L_10_C_7280f7fb, L_9_D_8c39df1c, L_13_RCO_37260826, L_12_MAX_MIN_34a3284e
  // also tied to GND on the sheet: {l_74191_counter_1_l_8_gnd_c4034234, l_74155_decoder_1_l_8_gnd_c4034234, l_74191_counter_2_l_8_gnd_c4034234}
  // also tied to VCC on the sheet: {l_74155_decoder_1_l_16_vcc_f510297a, l_74191_counter_1_l_16_vcc_f510297a, l_74191_counter_2_l_16_vcc_f510297a}
endmodule
